// Logisim project 3_inputs_impar.circ as structural Verilog: 1 circuit, main circuit main
module main (
  input  _00,
  input  _01,
  input  in_3,
  input  in_4,
  input  _10,
  input  _11,
  output out_7
);

  wire and_1_out, and_2_out, and_3_out, and_4_out, not_1_out, not_2_out;

  not not_1 (not_1_out, in_3);
  not not_2 (not_2_out, in_4);
  and and_1 (and_1_out, _00, not_1_out, not_2_out);
  and and_2 (and_2_out, _01, not_1_out, in_4);
  and and_3 (and_3_out, not_2_out, in_3, _10);
  and and_4 (and_4_out, in_3, in_4, _11);
  or or_1 (out_7, and_1_out, and_2_out, and_3_out, and_4_out);
endmodule
